# Fritzing sketch schematic (saved by Fritzing 0.9.10b)
breadboards: 1

parts:
  Barduino_ESP32 = Amica NodeMCU DEVKIT 1.0
  GY-521 = InvenSense MPU6050
  Ultrasonic = HC-SR04 Ultrasonic Distance Sensor
  Power = Battery

nets:
  N1: Barduino_ESP32.pin1, Barduino_ESP32.pin_10, Barduino_ESP32.pin_26
  GND: Barduino_ESP32.pin2, Barduino_ESP32.pin_9, Barduino_ESP32.pin_25, Barduino_ESP32.pin_29, GY-521.GND, Ultrasonic.GND, Power.-
  N2: Barduino_ESP32.pin_13, GY-521.SDA
  N3: Barduino_ESP32.pin_14, GY-521.SCL
  N4: Barduino_ESP32.pin_19, Ultrasonic.TRIG
  N5: Barduino_ESP32.pin_20, Ultrasonic.ECHO
  VCC: Barduino_ESP32.pin_30, GY-521.VCC, Ultrasonic.VCC, Power.+
